// Logisim project project.circ as structural Verilog: 8 circuits, main circuit main
module main (
);

  Register_File register_file_1 ();  // open: read, rd, rt, rs, rs_2, rt_2, rd_2, write, in_7, data2, data1
endmodule

// HA
module Half_Adder (
  input  Data1,
  input  Data2,
  output Sum,
  output CarryOut
);

  xor xor_1 (Sum, Data1, Data2);
  and and_1 (CarryOut, Data1, Data2);

  // Notes on the sheet:
  //   HALF ADDER
endmodule

// FA
module Full_Adder (
  input  Data1,
  input  Data2,
  input  Cin,
  output Sum,
  output Cout
);

  wire Half_Adder_2_carryout, Half_Adder_carryout, Half_Adder_sum;

  Half_Adder Half_Adder (.Data1(Data1), .Data2(Data2), .Sum(Half_Adder_sum), .CarryOut(Half_Adder_carryout));
  Half_Adder Half_Adder_2 (.Data1(Half_Adder_sum), .Data2(Cin), .Sum(Sum), .CarryOut(Half_Adder_2_carryout));
  or or_1 (Cout, Half_Adder_2_carryout, Half_Adder_carryout);

  // Notes on the sheet:
  //   Full Adder
endmodule

// Add
module Adder (
  input  [15:0] Data1,
  input  [15:0] Data2,
  output [15:0] Output
);

  wire full_adder_1_cout, full_adder_2_cout, full_adder_3_cout, full_adder_4_cout, full_adder_5_cout,
       full_adder_6_cout, full_adder_7_cout, full_adder_8_cout, full_adder_9_cout, full_adder_10_cout,
       full_adder_11_cout, full_adder_12_cout, full_adder_13_cout, full_adder_14_cout, full_adder_15_cout;

  Full_Adder full_adder_1 (.Data1(Data1[0]), .Data2(Data2[0]), .Cin(1'b0), .Sum(Output[0]), .Cout(full_adder_1_cout));
  Full_Adder full_adder_2 (
    .Data1(Data1[1]), .Data2(Data2[1]), .Cin(full_adder_1_cout), .Sum(Output[1]), .Cout(full_adder_2_cout));
  Full_Adder full_adder_3 (
    .Data1(Data1[2]), .Data2(Data2[2]), .Cin(full_adder_2_cout), .Sum(Output[2]), .Cout(full_adder_3_cout));
  Full_Adder full_adder_4 (
    .Data1(Data1[3]), .Data2(Data2[3]), .Cin(full_adder_3_cout), .Sum(Output[3]), .Cout(full_adder_4_cout));
  Full_Adder full_adder_5 (
    .Data1(Data1[4]), .Data2(Data2[4]), .Cin(full_adder_4_cout), .Sum(Output[4]), .Cout(full_adder_5_cout));
  Full_Adder full_adder_6 (
    .Data1(Data1[5]), .Data2(Data2[5]), .Cin(full_adder_5_cout), .Sum(Output[5]), .Cout(full_adder_6_cout));
  Full_Adder full_adder_7 (
    .Data1(Data1[6]), .Data2(Data2[6]), .Cin(full_adder_6_cout), .Sum(Output[6]), .Cout(full_adder_7_cout));
  Full_Adder full_adder_8 (
    .Data1(Data1[7]), .Data2(Data2[7]), .Cin(full_adder_7_cout), .Sum(Output[7]), .Cout(full_adder_8_cout));
  Full_Adder full_adder_9 (
    .Data1(Data1[8]), .Data2(Data2[8]), .Cin(full_adder_8_cout), .Sum(Output[8]), .Cout(full_adder_9_cout));
  Full_Adder full_adder_10 (
    .Data1(Data1[9]), .Data2(Data2[9]), .Cin(full_adder_9_cout), .Sum(Output[9]), .Cout(full_adder_10_cout));
  Full_Adder full_adder_11 (
    .Data1(Data1[10]), .Data2(Data2[10]), .Cin(full_adder_10_cout), .Sum(Output[10]),
    .Cout(full_adder_11_cout));
  Full_Adder full_adder_12 (
    .Data1(Data1[11]), .Data2(Data2[11]), .Cin(full_adder_11_cout), .Sum(Output[11]),
    .Cout(full_adder_12_cout));
  Full_Adder full_adder_13 (
    .Data1(Data1[12]), .Data2(Data2[12]), .Cin(full_adder_12_cout), .Sum(Output[12]),
    .Cout(full_adder_13_cout));
  Full_Adder full_adder_14 (
    .Data1(Data1[13]), .Data2(Data2[13]), .Cin(full_adder_13_cout), .Sum(Output[13]),
    .Cout(full_adder_14_cout));
  Full_Adder full_adder_15 (
    .Data1(Data1[14]), .Data2(Data2[14]), .Cin(full_adder_14_cout), .Sum(Output[14]),
    .Cout(full_adder_15_cout));
  Full_Adder full_adder_16 (
    .Data1(Data1[15]), .Data2(Data2[15]), .Cin(full_adder_15_cout), .Sum(Output[15]));  // open: Cout
endmodule

module ALU (
  input  [15:0] Data1,
  input  [15:0] Data2,
  input  [3:0] ALU_Control__from_opcode,
  output [15:0] out_4
);

  wire demultiplexer_1_out0, demultiplexer_1_out1, demultiplexer_1_out2, demultiplexer_1_out3,
       demultiplexer_1_out4, demultiplexer_1_out5, demultiplexer_1_out6, demultiplexer_1_out7,
       demultiplexer_1_out8, demultiplexer_1_out9;
  wire [3:0] controlled_buffer_8_out;
  wire [15:0] add_output, addi_output, and_1_out, controlled_buffer_4_out, controlled_buffer_5_out,
       controlled_buffer_6_out, controlled_buffer_7_out, controlled_buffer_9_out, controlled_buffer_10_out,
       controlled_buffer_12_out, controlled_buffer_13_out, controlled_buffer_14_out,
       controlled_buffer_15_out, controlled_buffer_16_out, controlled_buffer_17_out,
       controlled_buffer_18_out, controlled_buffer_19_out, controlled_buffer_20_out, multiplier_1_out,
       or_1_out, setlessthan_1_out_3, shifter_1_out, subtractor_1_output;

  Pull_Resistor pull_resistor_1 (.node(Data1));
  Pull_Resistor pull_resistor_2 (.node(Data1));
  Demultiplexer #(.select(4), .enable("false")) demultiplexer_1 (
    .out0(demultiplexer_1_out0), .out1(demultiplexer_1_out1), .out2(demultiplexer_1_out2),
    .out3(demultiplexer_1_out3), .out4(demultiplexer_1_out4), .out5(demultiplexer_1_out5),
    .out6(demultiplexer_1_out6), .out7(demultiplexer_1_out7), .out8(demultiplexer_1_out8),
    .out9(demultiplexer_1_out9), .in(1'b1), .sel(ALU_Control__from_opcode));  // open: out10, out11, out12, out13, out14, out15
  Controlled_Buffer #(.width(16)) controlled_buffer_1 (.en(demultiplexer_1_out8));  // open: in, out
  Controlled_Buffer #(.width(16)) controlled_buffer_2 (.en(demultiplexer_1_out9));  // open: in, out
  Controlled_Buffer #(.width(16)) controlled_buffer_3 (.en(demultiplexer_1_out9));  // open: in, out
  assign controlled_buffer_4_out = demultiplexer_1_out4 ? Data1 : 16'bz;  // Controlled_Buffer controlled_buffer_4
  assign controlled_buffer_5_out = demultiplexer_1_out5 ? Data1 : 16'bz;  // Controlled_Buffer controlled_buffer_5
  assign controlled_buffer_6_out = demultiplexer_1_out5 ? Data1 : 16'bz;  // Controlled_Buffer controlled_buffer_6
  assign controlled_buffer_7_out = demultiplexer_1_out6 ? Data1 : 16'bz;  // Controlled_Buffer controlled_buffer_7
  assign controlled_buffer_8_out = demultiplexer_1_out6 ? Data1[3:0] : 4'bz;  // Controlled_Buffer controlled_buffer_8
  assign controlled_buffer_9_out = demultiplexer_1_out7 ? Data1 : 16'bz;  // Controlled_Buffer controlled_buffer_9
  assign controlled_buffer_10_out = demultiplexer_1_out7 ? Data1 : 16'bz;  // Controlled_Buffer controlled_buffer_10
  Controlled_Buffer #(.width(16)) controlled_buffer_11 (.en(demultiplexer_1_out8));  // open: in, out
  assign controlled_buffer_12_out = demultiplexer_1_out0 ? Data1 : 16'bz;  // Controlled_Buffer controlled_buffer_12
  assign controlled_buffer_13_out = demultiplexer_1_out1 ? Data1 : 16'bz;  // Controlled_Buffer controlled_buffer_13
  assign controlled_buffer_14_out = demultiplexer_1_out1 ? Data1 : 16'bz;  // Controlled_Buffer controlled_buffer_14
  assign controlled_buffer_15_out = demultiplexer_1_out2 ? Data1 : 16'bz;  // Controlled_Buffer controlled_buffer_15
  assign controlled_buffer_16_out = demultiplexer_1_out2 ? Data1 : 16'bz;  // Controlled_Buffer controlled_buffer_16
  assign controlled_buffer_17_out = demultiplexer_1_out3 ? Data1 : 16'bz;  // Controlled_Buffer controlled_buffer_17
  assign controlled_buffer_18_out = demultiplexer_1_out3 ? Data1 : 16'bz;  // Controlled_Buffer controlled_buffer_18
  assign controlled_buffer_19_out = demultiplexer_1_out4 ? Data1 : 16'bz;  // Controlled_Buffer controlled_buffer_19
  assign controlled_buffer_20_out = demultiplexer_1_out0 ? Data1 : 16'bz;  // Controlled_Buffer controlled_buffer_20
  Pull_Resistor pull_resistor_3 (.node(controlled_buffer_6_out));
  Pull_Resistor pull_resistor_4 (.node(controlled_buffer_8_out));
  Pull_Resistor pull_resistor_5 (.node(controlled_buffer_5_out));
  Pull_Resistor pull_resistor_6 (.node(controlled_buffer_9_out));
  Pull_Resistor pull_resistor_7 (.node(controlled_buffer_10_out));
  Pull_Resistor pull_resistor_8 (.node(controlled_buffer_7_out));
  Pull_Resistor pull_resistor_9 (.node(controlled_buffer_17_out));
  Pull_Resistor pull_resistor_10 (.node(controlled_buffer_18_out));
  Pull_Resistor pull_resistor_11 (.node(controlled_buffer_19_out));
  Pull_Resistor pull_resistor_12 (.node(controlled_buffer_16_out));
  Pull_Resistor pull_resistor_13 (.node(controlled_buffer_14_out));
  Pull_Resistor pull_resistor_14 (.node(controlled_buffer_4_out));
  Pull_Resistor pull_resistor_15 (.node(controlled_buffer_15_out));
  Pull_Resistor pull_resistor_16 (.node(controlled_buffer_13_out));
  Pull_Resistor pull_resistor_17 (.node(controlled_buffer_12_out));
  Pull_Resistor pull_resistor_18 (.node(controlled_buffer_20_out));
  Adder add (.Data1(controlled_buffer_20_out), .Data2(controlled_buffer_12_out), .Output(add_output));
  Subtractor subtractor_1 (
    .Data1(controlled_buffer_13_out), .Data2(controlled_buffer_14_out), .Output(subtractor_1_output));
  Multiplier #(.width(16)) multiplier_1 (
    .a(controlled_buffer_15_out), .b(controlled_buffer_16_out), .out(multiplier_1_out));  // open: cin, cout
  assign and_1_out = controlled_buffer_17_out & controlled_buffer_18_out;  // AND_Gate and_1, 16 bits wide
  assign or_1_out = controlled_buffer_19_out | controlled_buffer_4_out;  // OR_Gate or_1, 16 bits wide
  Adder addi (.Data1(controlled_buffer_5_out), .Data2(controlled_buffer_6_out), .Output(addi_output));
  Shifter #(.width(16)) shifter_1 (.in(controlled_buffer_7_out), .\dist (controlled_buffer_8_out), .out(shifter_1_out));
  SetLessThan setlessthan_1 (
    .in_1(controlled_buffer_9_out), .in_2(controlled_buffer_10_out), .out_3(setlessthan_1_out_3));
  assign out_4 = add_output | subtractor_1_output | and_1_out | or_1_out | addi_output | shifter_1_out | setlessthan_1_out_3;  // OR_Gate or_2, 16 bits wide

  assign Data2 = Data1;
endmodule

// Sub
module Subtractor (
  input  [15:0] Data1,
  input  [15:0] Data2,
  output [15:0] Output
);

  wire full_adder_1_cout, full_adder_2_cout, full_adder_3_cout, full_adder_4_cout, full_adder_5_cout,
       full_adder_6_cout, full_adder_7_cout, full_adder_8_cout, full_adder_9_cout, full_adder_10_cout,
       full_adder_11_cout, full_adder_12_cout, full_adder_13_cout, full_adder_14_cout, full_adder_15_cout;
  wire [15:0] not_1_out;

  assign not_1_out = ~Data2;  // NOT_Gate not_1, 16 bits wide
  Full_Adder full_adder_1 (
    .Data1(Data1[0]), .Data2(not_1_out[0]), .Cin(1'b1), .Sum(Output[0]), .Cout(full_adder_1_cout));
  Full_Adder full_adder_2 (
    .Data1(Data1[1]), .Data2(not_1_out[1]), .Cin(full_adder_1_cout), .Sum(Output[1]), .Cout(full_adder_2_cout));
  Full_Adder full_adder_3 (
    .Data1(Data1[2]), .Data2(not_1_out[2]), .Cin(full_adder_2_cout), .Sum(Output[2]), .Cout(full_adder_3_cout));
  Full_Adder full_adder_4 (
    .Data1(Data1[3]), .Data2(not_1_out[3]), .Cin(full_adder_3_cout), .Sum(Output[3]), .Cout(full_adder_4_cout));
  Full_Adder full_adder_5 (
    .Data1(Data1[4]), .Data2(not_1_out[4]), .Cin(full_adder_4_cout), .Sum(Output[4]), .Cout(full_adder_5_cout));
  Full_Adder full_adder_6 (
    .Data1(Data1[5]), .Data2(not_1_out[5]), .Cin(full_adder_5_cout), .Sum(Output[5]), .Cout(full_adder_6_cout));
  Full_Adder full_adder_7 (
    .Data1(Data1[6]), .Data2(not_1_out[6]), .Cin(full_adder_6_cout), .Sum(Output[6]), .Cout(full_adder_7_cout));
  Full_Adder full_adder_8 (
    .Data1(Data1[7]), .Data2(not_1_out[7]), .Cin(full_adder_7_cout), .Sum(Output[7]), .Cout(full_adder_8_cout));
  Full_Adder full_adder_9 (
    .Data1(Data1[8]), .Data2(not_1_out[8]), .Cin(full_adder_8_cout), .Sum(Output[8]), .Cout(full_adder_9_cout));
  Full_Adder full_adder_10 (
    .Data1(Data1[9]), .Data2(not_1_out[9]), .Cin(full_adder_9_cout), .Sum(Output[9]),
    .Cout(full_adder_10_cout));
  Full_Adder full_adder_11 (
    .Data1(Data1[10]), .Data2(not_1_out[10]), .Cin(full_adder_10_cout), .Sum(Output[10]),
    .Cout(full_adder_11_cout));
  Full_Adder full_adder_12 (
    .Data1(Data1[11]), .Data2(not_1_out[11]), .Cin(full_adder_11_cout), .Sum(Output[11]),
    .Cout(full_adder_12_cout));
  Full_Adder full_adder_13 (
    .Data1(Data1[12]), .Data2(not_1_out[12]), .Cin(full_adder_12_cout), .Sum(Output[12]),
    .Cout(full_adder_13_cout));
  Full_Adder full_adder_14 (
    .Data1(Data1[13]), .Data2(not_1_out[13]), .Cin(full_adder_13_cout), .Sum(Output[13]),
    .Cout(full_adder_14_cout));
  Full_Adder full_adder_15 (
    .Data1(Data1[14]), .Data2(not_1_out[14]), .Cin(full_adder_14_cout), .Sum(Output[14]),
    .Cout(full_adder_15_cout));
  Full_Adder full_adder_16 (
    .Data1(Data1[15]), .Data2(not_1_out[15]), .Cin(full_adder_15_cout), .Sum(Output[15]));  // open: Cout
endmodule

// SLT
module SetLessThan (
  input  [15:0] in_1,
  input  [15:0] in_2,
  output [15:0] out_3
);

  wire comparator_1_lt;

  Comparator #(.width(16)) comparator_1 (.a(in_1), .b(in_2), .lt(comparator_1_lt));  // open: gt, eq
  assign out_3 = {{15{1'b0}}, comparator_1_lt};  // Bit_Extender bit_extender_1
endmodule

module Register_File (
  input  read,
  input  rd,
  input  rt,
  input  rs,
  input  rs_2,
  input  rt_2,
  input  [3:0] in_7,
  input  rd_2,
  input  write,
  output [3:0] data2,
  output [3:0] data1
);

  wire and_1_out, clock_1_out;
  wire [3:0] register_1_q;
  wire [3:3] rs_out, rt_out;

  Clock clock_1 (.out(clock_1_out));
  and u_rt (rt_out[3], rt, rt_2, read, clock_1_out);
  and u_rs (rs_out[3], rs, rs_2, read, clock_1_out);
  Register #(.width(4)) register_1 (.D(in_7), .Q(register_1_q), .clk(and_1_out));  // open: en, clr
  and and_1 (and_1_out, rd, rd_2, clock_1_out, write);
  assign data2 = {4{rt_out[3]}} & register_1_q;  // AND_Gate and_2, 4 bits wide
  assign data1 = {4{rs_out[3]}} & register_1_q;  // AND_Gate and_3, 4 bits wide
endmodule
